// Logisim project lab2.circ as structural Verilog: 1 circuit, main circuit main
module main (
  input  X3,
  input  X2,
  input  X1,
  input  X0,
  input  S0,
  input  S1,
  output O
);

  wire and_1_out, and_2_out, and_3_out, and_4_out, and_5_out, and_6_out, and_7_out, and_8_out,
       n4_to_1_mux_x2_74153_1_p8, not_1_out, not_2_out, not_3_out, not_4_out, or_1_out;

  not not_1 (not_1_out, X3);
  not not_2 (not_2_out, X2);
  and and_1 (and_1_out, not_1_out, X2);
  and and_2 (and_2_out, X3, not_2_out);
  and and_3 (and_3_out, not_1_out, not_2_out);
  or or_1 (or_1_out, and_3_out, and_4_out);
  and and_4 (and_4_out, X2, X3);
  // _4_to_1_MUX__x2___74153 #(.Facing("east")) 4_to_1_mux_x2_74153_1: pin names not known; wires that end beside it: or_1_out, and_2_out, and_1_out, or_1_out, 1'b0, X0, X1, n4_to_1_mux_x2_74153_1_p8
  not not_3 (not_3_out, n4_to_1_mux_x2_74153_1_p8);
  not not_4 (not_4_out, X0);
  and and_5 (and_5_out, not_3_out, not_4_out);
  and and_6 (and_6_out, n4_to_1_mux_x2_74153_1_p8, X0);
  and and_7 (and_7_out, not_4_out, n4_to_1_mux_x2_74153_1_p8);
  and and_8 (and_8_out, not_3_out, X0);
  // _4_to_1_MUX__x2___74153 #(.Facing("east")) 4_to_1_mux_x2_74153_2: pin names not known; wires that end beside it: and_5_out, and_6_out, and_7_out, and_8_out, 1'b0, S0, S1, O
endmodule
